# Fritzing sketch matrix_setup (saved by Fritzing 0.9.4)

parts:
  Mod1 = Raspberry Pi Pico
  Part1 = NeoPixel NeoMatrix 8x8 [part_number=1487]

nets:
  N1: Mod1.pin_6, Part1.VDD
  N2: Mod1.pin_38, Mod1.pin_42, Part1.GND
  N3: Mod1.pin_39, Part1.IN

custom parts:
  Raspberry Pi Pico: Raspberry Pi Pico. Based around the RP2040 microcontroller the Pico is a low cost microcontroller device bringing Raspberry Pi quality, cost, and easy of use to the microcontroller space. Jan 2021, Split part in to two versions: tht (this one) and SMD. This one will drill holes for a .1 in header in pcb to allow plugging in the module as well as providing pads to solder the module to the top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
  NeoPixel NeoMatrix 8x8: Put on your sunglasses before wiring up this LED matrix - 64 eye-blistering RGB LEDs adorn the NeoMatrix for a blast of configurable color. Arranged in an 8x8 matrix, each pixel is individually addressable. Only one microcontroller pin is required to control all the LEDs, and you get 24 bit color for each LED.
